// Logisim project control_logic.circ as structural Verilog: 1 circuit, main circuit control_logic
module control_logic (
  input  [31:0] inst,
  input  BrEq,
  input  BrLt,
  output PCSel,
  output RegWEn,
  output [2:0] ImmSel,
  output BrUn,
  output ASel,
  output BSel,
  output [3:0] ALUSel,
  output MemRW,
  output [1:0] WBSel
);

  wire and_1_out, and_2_out, and_3_out, and_4_out, and_5_out, and_6_out, and_7_out, and_8_out, and_9_out,
       and_10_out, and_11_out, and_12_out, and_13_out, and_14_out, and_15_out, and_16_out, and_17_out,
       and_18_out, and_19_out, and_20_out, and_21_out, and_22_out, and_23_out, and_24_out, comparator_8_eq,
       comparator_9_eq, comparator_21_eq, comparator_22_eq, func3_is_0, func3_is_1, func3_is_2, func3_is_3,
       func3_is_4, func3_is_5, func3_is_6, func3_is_7, func7_is_00, func7_is_01, func7_is_20, is_I_format,
       is_I_format_jalr, is_I_format_lblhlw, is_R_format, is_S_format, is_SB_format, is_U_format,
       is_UJ_format, or_3_out, or_4_out, or_5_out, or_6_out, or_7_out, or_8_out, or_9_out, or_10_out,
       or_11_out, or_12_out, or_13_out, or_14_out, or_15_out;
  wire [2:0] demultiplexer_19_out1, demultiplexer_20_out1;

  Comparator #(.width(7), .mode("unsigned")) comparator_1 (
    .a(inst[6:0]), .b(7'b1100011), .eq(is_SB_format));  // open: gt, lt
  Comparator #(.width(7), .mode("unsigned")) comparator_2 (
    .a(inst[6:0]), .b(7'b1100111), .eq(is_I_format_jalr));  // open: gt, lt
  Comparator #(.width(7), .mode("unsigned")) comparator_3 (
    .a(inst[6:0]), .b(7'b1101111), .eq(is_UJ_format));  // open: gt, lt
  Comparator #(.width(7), .mode("unsigned")) comparator_4 (
    .a(inst[6:0]), .b(7'b0110011), .eq(is_R_format));  // open: gt, lt
  Comparator #(.width(7), .mode("unsigned")) comparator_5 (
    .a(inst[6:0]), .b(7'b0000011), .eq(is_I_format_lblhlw));  // open: gt, lt
  Comparator #(.width(7), .mode("unsigned")) comparator_6 (
    .a(inst[6:0]), .b(7'b0010011), .eq(is_I_format));  // open: gt, lt
  Comparator #(.width(7), .mode("unsigned")) comparator_7 (
    .a(inst[6:0]), .b(7'b0100011), .eq(is_S_format));  // open: gt, lt
  Comparator #(.width(7), .mode("unsigned")) comparator_8 (
    .a(inst[6:0]), .b(7'b0010111), .eq(comparator_8_eq));  // open: gt, lt
  Comparator #(.width(7), .mode("unsigned")) comparator_9 (
    .a(inst[6:0]), .b(7'b0110111), .eq(comparator_9_eq));  // open: gt, lt
  or or_1 (is_U_format, comparator_8_eq, comparator_9_eq);
  or or_2 (PCSel, is_SB_format, is_I_format_jalr, is_UJ_format);
  Comparator #(.width(3), .mode("unsigned")) comparator_10 (
    .a(inst[14:12]), .b(3'b000), .eq(func3_is_0));  // open: gt, lt
  Comparator #(.width(3), .mode("unsigned")) comparator_11 (
    .a(inst[14:12]), .b(3'b001), .eq(func3_is_1));  // open: gt, lt
  Comparator #(.width(3), .mode("unsigned")) comparator_12 (
    .a(inst[14:12]), .b(3'b010), .eq(func3_is_2));  // open: gt, lt
  Comparator #(.width(3), .mode("unsigned")) comparator_13 (
    .a(inst[14:12]), .b(3'b011), .eq(func3_is_3));  // open: gt, lt
  Comparator #(.width(3), .mode("unsigned")) comparator_14 (
    .a(inst[14:12]), .b(3'b100), .eq(func3_is_4));  // open: gt, lt
  Comparator #(.width(3), .mode("unsigned")) comparator_15 (
    .a(inst[14:12]), .b(3'b101), .eq(func3_is_5));  // open: gt, lt
  Comparator #(.width(3), .mode("unsigned")) comparator_16 (
    .a(inst[14:12]), .b(3'b110), .eq(func3_is_6));  // open: gt, lt
  Comparator #(.width(3), .mode("unsigned")) comparator_17 (
    .a(inst[14:12]), .b(3'b111), .eq(func3_is_7));  // open: gt, lt
  Comparator #(.width(7), .mode("unsigned")) comparator_18 (
    .a(inst[31:25]), .b({7{1'b0}}), .eq(func7_is_00));  // open: gt, lt
  Comparator #(.width(7), .mode("unsigned")) comparator_19 (
    .a(inst[31:25]), .b(7'b0000001), .eq(func7_is_01));  // open: gt, lt
  Comparator #(.width(7), .mode("unsigned")) comparator_20 (
    .a(inst[31:25]), .b(7'b0100000), .eq(func7_is_20));  // open: gt, lt
  and and_1 (and_1_out, is_I_format, func3_is_0);
  and and_2 (and_2_out, func3_is_0, is_R_format, func7_is_00);
  and and_3 (and_3_out, func3_is_0, is_R_format, func7_is_01);
  and and_4 (and_4_out, func3_is_0, is_R_format, func7_is_20);
  and and_5 (and_5_out, func3_is_1, is_R_format, func7_is_00);
  and and_6 (and_6_out, func3_is_1, is_I_format, func7_is_00);
  and and_7 (and_7_out, func3_is_1, is_R_format, func7_is_01);
  and and_8 (and_8_out, func3_is_3, is_R_format, func7_is_00);
  and and_9 (and_9_out, is_I_format, func3_is_2);
  and and_10 (and_10_out, func3_is_2, is_R_format, func7_is_00);
  and and_11 (and_11_out, is_I_format, func3_is_4);
  and and_12 (and_12_out, func3_is_4, is_R_format, func7_is_00);
  Demultiplexer #(.width(4), .enable("false")) demultiplexer_1 (
    .out1(ALUSel), .in(4'b1010), .sel(and_3_out));  // open: out0
  Demultiplexer #(.width(4), .enable("false")) demultiplexer_2 (
    .out1(ALUSel), .in(4'b1100), .sel(and_4_out));  // open: out0
  Demultiplexer #(.width(4), .enable("false")) demultiplexer_3 (
    .out1(ALUSel), .in(4'b0110), .sel(or_3_out));  // open: out0
  or or_3 (or_3_out, and_5_out, and_6_out);
  Demultiplexer #(.width(4), .enable("false")) demultiplexer_4 (
    .out1(ALUSel), .in(4'b1110), .sel(and_7_out));  // open: out0
  Demultiplexer #(.width(4), .enable("false")) demultiplexer_5 (
    .out1(ALUSel), .in(4'b1011), .sel(and_8_out));  // open: out0
  or or_4 (or_4_out, and_9_out, and_10_out);
  Demultiplexer #(.width(4), .enable("false")) demultiplexer_6 (
    .out1(ALUSel), .in(4'b0000), .sel(or_5_out));  // open: out0
  or or_5 (or_5_out, and_1_out, and_2_out);
  Demultiplexer #(.width(4), .enable("false")) demultiplexer_7 (
    .out1(ALUSel), .in(4'b0111), .sel(or_4_out));  // open: out0
  Demultiplexer #(.width(4), .enable("false")) demultiplexer_8 (
    .out1(ALUSel), .in(4'b0011), .sel(or_6_out));  // open: out0
  or or_6 (or_6_out, and_11_out, and_12_out);
  and and_13 (and_13_out, func3_is_5, is_I_format, func7_is_00);
  and and_14 (and_14_out, func3_is_5, is_R_format, func7_is_00);
  and and_15 (and_15_out, func3_is_5, is_R_format, func7_is_20);
  and and_16 (and_16_out, func3_is_5, is_I_format, func7_is_20);
  Demultiplexer #(.width(4), .enable("false")) demultiplexer_9 (
    .out1(ALUSel), .in(4'b1000), .sel(and_17_out));  // open: out0
  and and_17 (and_17_out, func3_is_5, is_R_format, func7_is_01);
  or or_7 (or_7_out, and_13_out, and_14_out);
  or or_8 (or_8_out, and_15_out, and_16_out);
  and and_18 (and_18_out, is_I_format, func3_is_6);
  and and_19 (and_19_out, func3_is_6, is_R_format, func7_is_00);
  and and_20 (and_20_out, is_I_format, func3_is_7);
  and and_21 (and_21_out, func3_is_7, is_R_format, func7_is_01);
  Demultiplexer #(.width(4), .enable("false")) demultiplexer_10 (
    .out1(ALUSel), .in(4'b0001), .sel(and_22_out));  // open: out0
  and and_22 (and_22_out, func3_is_7, is_R_format, func7_is_00);
  Demultiplexer #(.width(4), .enable("false")) demultiplexer_11 (
    .out1(ALUSel), .in(4'b0100), .sel(or_7_out));  // open: out0
  Demultiplexer #(.width(4), .enable("false")) demultiplexer_12 (
    .out1(ALUSel), .in(4'b0101), .sel(or_8_out));  // open: out0
  Demultiplexer #(.width(4), .enable("false")) demultiplexer_13 (
    .out1(ALUSel), .in(4'b0010), .sel(or_9_out));  // open: out0
  or or_9 (or_9_out, and_18_out, and_19_out);
  or or_10 (or_10_out, and_20_out, and_21_out);
  Demultiplexer #(.width(4), .enable("false")) demultiplexer_14 (
    .out1(ALUSel), .in(4'b1001), .sel(or_10_out));  // open: out0
  or or_11 (or_11_out, is_SB_format, is_I_format_jalr, is_UJ_format, is_I_format_lblhlw, is_S_format);
  Demultiplexer #(.width(4), .enable("false")) demultiplexer_15 (
    .out1(ALUSel), .in(4'b0000), .sel(or_11_out));  // open: out0
  Multiplexer #(.enable("false")) multiplexer_1 (.in0(1'b0), .in1(1'b1), .out(MemRW), .sel(is_S_format));
  or or_12 (or_12_out, is_I_format_jalr, is_UJ_format);
  or or_13 (or_13_out, is_R_format, is_I_format, is_U_format);
  Multiplexer #(.enable("false")) multiplexer_2 (.in0(1'b1), .in1(1'b0), .out(RegWEn), .sel(or_14_out));
  or or_14 (or_14_out, is_S_format, is_SB_format);
  Demultiplexer #(.width(2), .enable("false")) demultiplexer_16 (
    .out1(WBSel), .in(2'b00), .sel(or_12_out));  // open: out0
  Demultiplexer #(.width(2), .enable("false")) demultiplexer_17 (
    .out1(WBSel), .in(2'b01), .sel(or_13_out));  // open: out0
  Demultiplexer #(.width(2), .enable("false")) demultiplexer_18 (
    .out1(WBSel), .in(2'b10), .sel(is_I_format_lblhlw));  // open: out0
  Multiplexer #(.enable("false")) multiplexer_3 (.in0(1'b0), .in1(1'b1), .out(ASel), .sel(or_15_out));
  or or_15 (or_15_out, is_SB_format, is_UJ_format, is_U_format);
  Multiplexer #(.enable("false")) multiplexer_4 (.in0(1'b1), .in1(1'b0), .out(BSel), .sel(is_R_format));
  Demultiplexer #(.width(3), .enable("false")) demultiplexer_19 (
    .out1(demultiplexer_19_out1), .in(inst[14:12]), .sel(is_SB_format));  // open: out0
  Demultiplexer #(.width(3), .enable("false")) demultiplexer_20 (
    .out1(demultiplexer_20_out1), .in(inst[14:12]), .sel(is_SB_format));  // open: out0
  Demultiplexer #(.width(3), .enable("false")) demultiplexer_21 (
    .out1(ImmSel), .in(3'b000), .sel(is_I_format));  // open: out0
  Demultiplexer #(.width(3), .enable("false")) demultiplexer_22 (
    .out1(ImmSel), .in(3'b001), .sel(is_S_format));  // open: out0
  Demultiplexer #(.width(3), .enable("false")) demultiplexer_23 (
    .out1(ImmSel), .in(3'b010), .sel(is_SB_format));  // open: out0
  Demultiplexer #(.width(3), .enable("false")) demultiplexer_24 (
    .out1(ImmSel), .in(3'b011), .sel(is_U_format));  // open: out0
  Demultiplexer #(.width(3), .enable("false")) demultiplexer_25 (
    .out1(ImmSel), .in(3'b100), .sel(is_UJ_format));  // open: out0
  Comparator #(.width(3), .mode("unsigned")) comparator_21 (
    .a(demultiplexer_19_out1), .b(3'b100), .eq(comparator_21_eq));  // open: gt, lt
  Comparator #(.width(3), .mode("unsigned")) comparator_22 (
    .a(demultiplexer_20_out1), .b(3'b110), .eq(comparator_22_eq));  // open: gt, lt
  and and_23 (and_23_out, comparator_21_eq, is_SB_format);
  and and_24 (and_24_out, comparator_22_eq, is_SB_format);
  Demultiplexer #(.enable("false")) demultiplexer_26 (.out1(BrUn), .in(1'b0), .sel(and_23_out));  // open: out0
  Demultiplexer #(.enable("false")) demultiplexer_27 (.out1(BrUn), .in(1'b1), .sel(and_24_out));  // open: out0

  // Other names for the same wires on the sheet: opcode[6:0] = inst[6:0]; func3[2:0] = inst[14:12];
  //   func7[6:0] = inst[31:25]

  // Notes on the sheet:
  //   INPUTS to your circuit
  //   DON'T CHANGE THE LOCATIONS OF THE INPUTS AND OUTPUTS!
  //   OUTPUT from your circuit
  //   default value is 0
  //   Except S and SB format, all formats need to set RegWen as 1(Y)
  //   Default value is 0(read), because we do not want to accidently write in to memory
endmodule
