// Logisim project imm_gen.circ as structural Verilog: 1 circuit, main circuit imm_gen
module imm_gen (
  input  [31:0] inst,
  input  [2:0] ImmSel,
  output [31:0] imm
);

  wire [31:11] I_format, S_format;
  wire [31:12] SB_format;
  wire [31:31] undriven;

  assign I_format = {{20{inst[31]}}, inst[31]};  // Bit_Extender bit_extender_1
  assign S_format = {{20{inst[31]}}, inst[31]};  // Bit_Extender bit_extender_2
  assign SB_format = {{19{undriven[31]}}, undriven[31]};  // Bit_Extender bit_extender_3
  Multiplexer #(.select(3), .width(32), .enable("false")) multiplexer_1 (
    .in0({I_format, inst[30:20]}), .in1({S_format, inst[30:25], inst[11:7]}), .out(imm), .sel(ImmSel));  // open: in2, in3, in4, in5, in6, in7

  // Other names for the same wires on the sheet: I_format[10:0] = inst[30:20];
  //   S_format[10:0] = {inst[30:25], inst[11:7]}

  // Notes on the sheet:
  //   INPUTS to your circuit
  //   DON'T CHANGE THE LOCATIONS OF THE INPUTS AND OUTPUTS!
  //   OUTPUT from your circuit
endmodule
